# Fritzing sketch OSDMenu (saved by Fritzing 0.8.7b)
stripboards: 6
breadboards: 4
perfboards: 7

parts:
  J94 = male pin header, 6 pins [form="♂ (male)"]
  S16 = Pushbutton [package="[THT]"]
  S17 = Pushbutton [package="[THT]"]
  S18 = Pushbutton [package="[THT]"]
  S19 = Pushbutton [package="[THT]"]
  S20 = Pushbutton [package="[THT]"]
  U7 = Optocoupler [package=THT]
  U8 = Optocoupler [package=THT]
  U9 = Optocoupler [package=THT]
  U10 = Optocoupler [package=THT]
  U11 = Optocoupler [package=THT]
  U12 = Optocoupler [package=THT]
  U13 = Optocoupler [package=THT]
  U14 = Optocoupler [package=THT]
  U15 = Optocoupler [package=THT]
  U16 = Optocoupler [package=THT]
  U17 = Optocoupler [package=THT]
  U18 = Optocoupler [package=THT]
  U19 = Optocoupler [package=THT]
  U20 = Optocoupler [package=THT]
  Part11 = Arduino Uno (Rev3)
  R7 = Resistor [tolerance=±5% resistance=4.7k package=THT]
  R8 = Resistor [tolerance=±5% resistance=4.7k package=THT]
  R9 = Resistor [tolerance=±5% resistance=4.7k package=THT]
  Q3 = NPN-Transistor [package="TO92 [THT]"]
  Q2 = NPN-Transistor [package="TO92 [THT]"]
  Q4 = NPN-Transistor [package="TO92 [THT]"]
  U6 = Optocoupler [part_number=4N25 package=THT]
  R12 = Resistor [tolerance=±5% resistance=330 package=THT]
  R13 = Resistor [tolerance=±5% resistance=330 package=THT]
  R14 = Resistor [tolerance=±5% resistance=330 package=THT]
  R15 = Resistor [tolerance=±5% resistance=330 package=THT]
  R16 = Resistor [tolerance=±5% resistance=330 package=THT]
  R17 = Resistor [tolerance=±5% resistance=330 package=THT]
  R18 = Resistor [tolerance=±5% resistance=330 package=THT]
  R19 = Resistor [tolerance=±5% resistance=330 package=THT]
  R20 = Resistor [tolerance=±5% resistance=330 package=THT]
  R21 = Resistor [tolerance=±5% resistance=330 package=THT]
  R22 = Resistor [tolerance=±5% resistance=330 package=THT]
  R23 = Resistor [tolerance=±5% resistance=330 package=THT]
  R24 = Resistor [tolerance=±5% resistance=330 package=THT]
  R25 = Resistor [tolerance=±5% resistance=330 package=THT]
  R26 = Resistor [tolerance=±5% resistance=330 package=THT]
  J97 = screw terminal, 6 pins
  J105 = screw terminal, 6 pins
  J106 = screw terminal, 6 pins
  LED10 = LED - 5mm [color="Blue (470nm)" package="5 mm [THT]"]
  R28 = Resistor [tolerance=±5% resistance=330 package=THT]
  LED11 = LED - 5mm [color="Blue (470nm)" package="5 mm [THT]"]
  R29 = Resistor [tolerance=±5% resistance=330 package=THT]
  LED12 = LED - 5mm [color="Blue (470nm)" package="5 mm [THT]"]
  R30 = Resistor [tolerance=±5% resistance=330 package=THT]
  R31 = Resistor [tolerance=±5% resistance=10k package=THT]
  R32 = Resistor [tolerance=±5% resistance=10k package=THT]
  J107 = Screw terminal - 2 pins [package=THT]
  J108 = Screw terminal - 2 pins [package=THT]
  J109 = Screw terminal - 2 pins [package=THT]
  J110 = Screw terminal - 2 pins [package=THT]
  J111 = Screw terminal - 2 pins [package=THT]
  LED13 = LED - 5mm [color="Green (555nm)" package="5 mm [THT]"]
  R33 = Resistor [tolerance=±5% resistance=330 package=THT]
  LED14 = LED - 5mm [color="Green (555nm)" package="5 mm [THT]"]
  R34 = Resistor [tolerance=±5% resistance=330 package=THT]
  LED15 = LED - 5mm [color="Green (555nm)" package="5 mm [THT]"]
  R35 = Resistor [tolerance=±5% resistance=330 package=THT]

nets:
  N1: J94.pin1, S16.Pin_3, S16.Pin_4, Part11.D9_PWM
  N2: J94.pin2, S17.Pin_1, S17.Pin_2, Part11.D10_PWM/SS
  N3: J94.pin3, S20.Pin_1, S20.Pin_2, Part11.D11_PWM/MOSI
  N4: J94.pin4, S19.Pin_1, S19.Pin_2, Part11.D12/MISO
  N5: J94.pin5, S18.Pin_1, S18.Pin_2, Part11.D13/SCK
  N6: J94.pin6, S16.Pin_1, S16.Pin_2, S17.Pin_3, S17.Pin_4, S18.Pin_3, S18.Pin_4, S19.Pin_3, S19.Pin_4, S20.Pin_3, S20.Pin_4, Part11.GND, Q3.E, Q2.E, Q4.E, R31.Pin_0, J108.pin2
  N7: U7.Pin_1, U12.Pin_1, U17.Pin_1, Part11.D6_PWM
  N8: U7.Pin_2, R13.Pin_1
  N9: U7.Pin_4, U8.Pin_4, U9.Pin_4, U10.Pin_4, U6.Pin_4, J97.pin6
  N10: U7.Pin_5, J97.pin2
  N11: U8.Pin_1, U13.Pin_1, U18.Pin_1, Part11.D4
  N12: U8.Pin_2, R15.Pin_1
  N13: U8.Pin_5, J97.pin4
  N14: U9.Pin_1, U14.Pin_1, U19.Pin_1, Part11.D3_PWM
  N15: U9.Pin_2, R16.Pin_1
  N16: U9.Pin_5, J97.pin5
  N17: U10.Pin_1, U15.Pin_1, U20.Pin_1, Part11.D5_PWM
  N18: U10.Pin_2, R14.Pin_1
  N19: U10.Pin_5, J97.pin3
  N20: U11.Pin_1, U16.Pin_1, Part11.D7, U6.Pin_1
  N21: U11.Pin_2, R21.Pin_1
  N22: U11.Pin_4, U12.Pin_4, U13.Pin_4, U14.Pin_4, U15.Pin_4, J105.pin6
  N23: U11.Pin_5, J105.pin1
  N24: U12.Pin_2, R20.Pin_1
  N25: U12.Pin_5, J105.pin2
  N26: U13.Pin_2, R17.Pin_1
  N27: U13.Pin_5, J105.pin4
  N28: U14.Pin_2, R18.Pin_1
  N29: U14.Pin_5, J105.pin5
  N30: U15.Pin_2, R19.Pin_1
  N31: U15.Pin_5, J105.pin3
  N32: U16.Pin_2, R26.Pin_1
  N33: U16.Pin_4, U17.Pin_4, U18.Pin_4, U19.Pin_4, U20.Pin_4, J106.pin6
  N34: U16.Pin_5, J106.pin1
  N35: U17.Pin_2, R25.Pin_1
  N36: U17.Pin_5, J106.pin2
  N37: U18.Pin_2, R22.Pin_1
  N38: U18.Pin_5, J106.pin4
  N39: U19.Pin_2, R23.Pin_1
  N40: U19.Pin_5, J106.pin5
  N41: U20.Pin_2, R24.Pin_1
  N42: U20.Pin_5, J106.pin3
  N43: Part11.A0, R9.Pin_0
  N44: Part11.A1, R8.Pin_0
  N45: Part11.A2, R7.Pin_0
  N46: Part11.A3, R33.Pin_0
  N47: Part11.A4/SDA, R34.Pin_0
  N48: Part11.A5/SCL, R35.Pin_0
  N49: Part11.D8, R32.Pin_0, J108.pin1
  N50: Part11.D2, R31.Pin_1, J107.pin2
  N51: Part11.5V, R28.Pin_0, R29.Pin_0, R30.Pin_0, R32.Pin_1, J107.pin1, LED13.anode, LED14.anode, LED15.anode
  N52: R7.Pin_1, Q4.B
  N53: R8.Pin_1, Q3.B
  N54: R9.Pin_1, Q2.B
  N55: Q3.C, R17.Pin_0, R18.Pin_0, R19.Pin_0, R20.Pin_0, R21.Pin_0, LED11.cathode
  N56: Q2.C, R22.Pin_0, R23.Pin_0, R24.Pin_0, R25.Pin_0, R26.Pin_0, LED12.cathode
  N57: Q4.C, R12.Pin_0, R13.Pin_0, R14.Pin_0, R15.Pin_0, R16.Pin_0, LED10.cathode
  N58: U6.Pin_2, R12.Pin_1
  N59: U6.Pin_5, J97.pin1
  N60: LED10.anode, R28.Pin_1
  N61: LED11.anode, R29.Pin_1
  N62: LED12.anode, R30.Pin_1
  N63: J109.pin2, J110.pin2, J111.pin2
  N64: LED13.cathode, R33.Pin_1
  N65: LED14.cathode, R34.Pin_1
  N66: LED15.cathode, R35.Pin_1

notes:
  BC337 NPN
  C33725 W73
  C-B-E
  using pull-up resistors:
  pinMode(buttonPin, INPUT);
  digitalWrite(buttonPin, HIGH);
  18x R=330
  2x R=10K
  3x R=4K7
