# Fritzing sketch scb2kControl (saved by Fritzing 0.7.12b)
stripboards: 24

parts:
  CONTATOR11 = IC, DIP package, 10 pins [chip_label=CONTATOR]  # not connected
  J79 = screw terminal, 3 pins  # not connected
  J80 = screw terminal, 3 pins  # not connected
  J81 = screw terminal, 7 pins  # not connected
  J82 = male pin header, 2 pins [form="♂ (male)"]  # not connected
  J84 = female pin header, 14 pins [form="♀ (female)"]  # not connected
  J85 = female pin header, 14 pins [form="♀ (female)"]  # not connected
  J88 = screw terminal, 5 pins  # not connected
  J89 = screw terminal, 3 pins  # not connected
  LED5 = Super Flux LED blue [color=Blue]  # not connected
  LED6 = Super Flux LED blue [color=Blue]  # not connected
  S6 = Pushbutton [package="[THT]"]
  S7 = Pushbutton [package="[THT]"]
  S8 = Pushbutton [package="[THT]"]
  S9 = Pushbutton [package="[THT]"]
  S10 = Pushbutton [package="[THT]"]
  J91 = male pin header, 6 pins [form="♂ (male)"]  # not connected
  J92 = male pin header, 6 pins [form="♂ (male)"]  # not connected
  U1 = Optocoupler [package=THT]  # not connected
  IC1 = ULN2803A [package=THT]  # not connected
  U2 = Optocoupler [package=THT]  # not connected
  U3 = Optocoupler [package=THT]  # not connected
  U4 = Optocoupler [package=THT]  # not connected
  U5 = Optocoupler [package=THT]  # not connected
  S11 = Pushbutton [package="[THT]"]
  S12 = Pushbutton [package="[THT]"]
  S13 = Pushbutton [package="[THT]"]
  S14 = Pushbutton [package="[THT]"]
  S15 = Pushbutton [package="[THT]"]
  J93 = male pin header, 6 pins [form="♂ (male)"]

nets:
  N1: S6.Pin_1, S6.Pin_2, S7.Pin_3, S7.Pin_4, S8.Pin_1, S8.Pin_2, S9.Pin_1, S9.Pin_2
  N2: S6.Pin_3, S6.Pin_4
  N3: S7.Pin_1, S7.Pin_2
  N4: S8.Pin_3, S8.Pin_4
  N5: S9.Pin_3, S9.Pin_4
  N6: S10.Pin_1, S10.Pin_2
  N7: S10.Pin_3, S10.Pin_4
  N8: S11.Pin_1, S11.Pin_2, J93.pin3
  N9: S11.Pin_3, S11.Pin_4, S12.Pin_3, S12.Pin_4, S13.Pin_3, S13.Pin_4, S14.Pin_3, S14.Pin_4, S15.Pin_1, S15.Pin_2, J93.pin6
  N10: S12.Pin_1, S12.Pin_2, J93.pin4
  N11: S13.Pin_1, S13.Pin_2, J93.pin5
  N12: S14.Pin_1, S14.Pin_2, J93.pin2
  N13: S15.Pin_3, S15.Pin_4, J93.pin1
